# Fritzing sketch hygrometer (saved by Fritzing 0.9.3b)
breadboards: 1

parts:
  Part1 = Arduino Pro Mini (5V)
  DHT2 = DHT11 Humitidy and Temperature Sensor
  OLED_I2C1 = OLED 128x64 I2C Monochrome Display
  R1 = Resistor [tolerance=±5% resistance=10k package=THT]
  4x_AA_battery = DC Power [voltage=6V]

nets:
  N1: Part1.VCC, 4x_AA_battery.V+
  GND: Part1.GND, DHT2.GND, OLED_I2C1.GND, 4x_AA_battery.V-
  N2: Part1.A4, OLED_I2C1.SDA
  N3: Part1.A5, OLED_I2C1.SCL
  N4: Part1.D9, DHT2.DATA, R1.Pin_1
  VDD: Part1.D5, DHT2.VDD, OLED_I2C1.VDD, R1.Pin_0

custom parts:
  DHT11 Humitidy and Temperature Sensor: DHT11 Humidity and Temperature Sensor
